# Fritzing sketch 小车 (saved by Fritzing 0.9.3b)
breadboards: 1

parts:
  元件1 = Arduino Mega 2560 (Rev3)
  M1 = Getriebemotor
  M2 = Getriebemotor
  M3 = Getriebemotor  # not connected
  元件3 = Adafruit ESP32-S3 Feather [part_number="Adafruit #5323"]
  J1 = Basic Servo
  e-radionica1 = TCS230 Color Sensor [part_number=101209]
  HC-SR04_Sensor_1 = HC-SR04 Ultrasonic Distance Sensor
  HC-SR04_Sensor_2 = HC-SR04 Ultrasonic Distance Sensor

nets:
  N1: 元件1.A8, e-radionica1.Out
  N2: 元件1.A9, e-radionica1.S2
  N3: 元件1.A10, e-radionica1.S3
  GND: 元件1.GND, 元件3.GND, HC-SR04_Sensor_1.GND, HC-SR04_Sensor_2.GND
  N4: 元件1.D8_PWM, M2.pin_2
  3V3: 元件1.3V3, 元件3.3.3V
  VCC: 元件1.5V, HC-SR04_Sensor_1.VCC, HC-SR04_Sensor_2.VCC
  N5: 元件1.D0_RX0, 元件3.TX
  N6: 元件1.D1_TX0, 元件3.RX
  N7: 元件1.D6_PWM, M1.pin_2
  N8: 元件1.D31, HC-SR04_Sensor_1.TRIG
  N9: 元件1.D33, HC-SR04_Sensor_1.ECHO
  N10: 元件1.D35, HC-SR04_Sensor_2.TRIG
  N11: 元件1.D37, HC-SR04_Sensor_2.ECHO
  N12: 元件1.D53, J1.pulse
  GND_2: M1.pin_1, J1.gnd, e-radionica1.Gnd
  VCC_2: J1.vcc, e-radionica1.Vcc

custom parts:
  Adafruit ESP32-S3 Feather: The ESP32-S3 has arrived in Feather format - and what a great way to get started with this powerful new chip from Espressif! With dual 240 MHz cores, WiFi and BLE support, and native USB, this Feather is great for powering your IoT projects. That's right - it's the new Adafruit ESP32-S3 Feather! With native USB and 8 MB flash, this board will let you upgrade your existing ESP32 projects.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
  TCS230 Color Sensor: TCS230
